// Digital circuit CMD DEC.dig as structural Verilog
module CMD_DEC (
  input  [7:0] CMD_IN,
  input  [7:0] CMD_CMP,
  output CMD_EN
);

  Comparator #(.Bits(8)) comparator_1 (.a(CMD_IN), .b(CMD_CMP), .eq(CMD_EN));  // open: gt, lt
endmodule
