// Digital circuit 8 By 8 Pixel Display.dig as structural Verilog
module _8_By_8_Pixel_Display (
  input  [7:0] CMD,
  input  [7:0] DAT,
  input  [15:0] ADR,
  input  CLK
);

  Comparator comparator_1 (.b(1'b1));  // open: a, gt, eq, lt
  // Register register_1: pin names not known

  // Notes on the sheet:
  //   CLK
  //   DAT
  //   ADR
endmodule
