// Digital circuit CPU.dig as structural Verilog
module CPU (
  input  CLR_PC,
  input  STR,
  input  clk
);

  wire alu_1_dat_dis, comparator_1_eq, comparator_2_eq, comparator_3_eq, comparator_4_eq, comparator_5_eq,
       comparator_6_eq, comparator_7_eq, comparator_8_eq, comparator_9_eq, comparator_10_eq,
       comparator_11_eq, diodeforward_1_out;
  wire [3:0] register_2_val, register_2_val_2;
  wire [7:0] _8_by_8_pixel_display_1_out_0, _8_by_8_pixel_display_1_out_1, _8_by_8_pixel_display_1_out_2,
       _8_by_8_pixel_display_1_out_3, _8_by_8_pixel_display_1_out_4, _8_by_8_pixel_display_1_out_5,
       _8_by_8_pixel_display_1_out_6, _8_by_8_pixel_display_1_out_7, dipswitch_1_out, flash_memory_1_q_cmd,
       flash_memory_1_q_dat, register_1_val;
  wire [15:0] flash_memory_1_q_adr, programme_counter_1_ln;

  LED led_1 (.in(register_1_val[7]));
  LED led_2 (.in(register_1_val[6]));
  DipSwitch dipswitch_1 (.out(dipswitch_1_out[7]));
  DipSwitch dipswitch_2 (.out(dipswitch_1_out[6]));
  LED led_3 (.in(register_1_val[5]));
  LED led_4 (.in(register_1_val[4]));
  DipSwitch dipswitch_3 (.out(dipswitch_1_out[5]));
  DipSwitch dipswitch_4 (.out(dipswitch_1_out[4]));
  LED led_5 (.in(register_1_val[3]));
  LED led_6 (.in(register_1_val[2]));
  DipSwitch dipswitch_5 (.out(dipswitch_1_out[3]));
  DipSwitch dipswitch_6 (.out(dipswitch_1_out[2]));
  LED led_7 (.in(register_1_val[1]));
  LED led_8 (.in(register_1_val[0]));
  DipSwitch dipswitch_7 (.out(dipswitch_1_out[1]));
  DipSwitch dipswitch_8 (.out(dipswitch_1_out[0]));
  Comparator #(.Bits(8)) comparator_1 (.a(flash_memory_1_q_cmd), .b(8'h1), .eq(comparator_1_eq));  // open: gt, lt
  Comparator #(.Bits(8)) comparator_2 (.a(flash_memory_1_q_cmd), .b(8'h2), .eq(comparator_2_eq));  // open: gt, lt
  Comparator #(.Bits(8)) comparator_3 (.a(flash_memory_1_q_cmd), .b(8'h3), .eq(comparator_3_eq));  // open: gt, lt
  Comparator #(.Bits(8)) comparator_4 (.a(flash_memory_1_q_cmd), .b(8'h4), .eq(comparator_4_eq));  // open: gt, lt
  Comparator #(.Bits(8)) comparator_5 (.a(flash_memory_1_q_cmd), .b(8'h5), .eq(comparator_5_eq));  // open: gt, lt
  Comparator #(.Bits(8)) comparator_6 (.a(flash_memory_1_q_cmd), .b(8'h6), .eq(comparator_6_eq));  // open: gt, lt
  Comparator #(.Bits(8)) comparator_7 (.a(flash_memory_1_q_cmd), .b(8'h7), .eq(comparator_7_eq));  // open: gt, lt
  Comparator #(.Bits(8)) comparator_8 (.a(flash_memory_1_q_cmd), .b(8'h26), .eq(comparator_8_eq));  // open: gt, lt
  Comparator #(.Bits(8)) comparator_9 (.a(flash_memory_1_q_cmd), .b(8'h27), .eq(comparator_9_eq));  // open: gt, lt
  Comparator #(.Bits(8)) comparator_10 (.a(flash_memory_1_q_cmd), .b(8'h28), .eq(comparator_10_eq));  // open: gt, lt
  Comparator #(.Bits(8)) comparator_11 (.a(flash_memory_1_q_cmd), .b(8'h29), .eq(comparator_11_eq));  // open: gt, lt
  DiodeForward diodeforward_1 (.in(comparator_7_eq), .out(diodeforward_1_out));
  DiodeForward diodeforward_2 (.in(comparator_8_eq), .out(diodeforward_1_out));
  DiodeForward diodeforward_3 (.in(comparator_9_eq), .out(diodeforward_1_out));
  DiodeForward diodeforward_4 (.in(comparator_11_eq), .out(diodeforward_1_out));
  PullDown pulldown_1 (.out(diodeforward_1_out));
  Programme_Counter programme_counter_1 (
    .DAT(flash_memory_1_q_dat), .ADR(flash_memory_1_q_adr), .CLK(clk), .JMP(comparator_1_eq),
    .CJP(comparator_2_eq), .CLR(CLR_PC), .LN(programme_counter_1_ln));
  Flash_Memory flash_memory_1 (
    .LN(programme_counter_1_ln), .DAT_dis(diodeforward_1_out), .ADR_dis(comparator_5_eq), .CLK(clk),
    .Q_CMD(flash_memory_1_q_cmd), .Q_DAT(flash_memory_1_q_dat), .Q_ADR(flash_memory_1_q_adr));
  ALU alu_1 (
    .CMD(flash_memory_1_q_cmd), .DAT(flash_memory_1_q_dat), .CLK(clk), .Q(flash_memory_1_q_dat),
    .DAT_dis(alu_1_dat_dis));
  DiodeForward diodeforward_5 (.in(alu_1_dat_dis), .out(diodeforward_1_out));
  DAT_to_ADR_interface dat_to_adr_interface_1 (
    .DAT(flash_memory_1_q_dat), .STR_1(comparator_3_eq), .STR_2(comparator_4_eq), .LD(comparator_5_eq),
    .CLK(clk), .ADR(flash_memory_1_q_adr));
  RAM ram_1 (
    .DAT(flash_memory_1_q_dat), .ADR(flash_memory_1_q_adr), .STR(comparator_6_eq), .LD(comparator_7_eq),
    .CLK(clk), .Q(flash_memory_1_q_dat));
  Register register_1 (
    .D(dipswitch_1_out), .STR(STR), .LD(comparator_8_eq), .CLK(clk), .VAL(register_1_val),
    .Q(flash_memory_1_q_dat));
  Input_Control input_control_1 (.INP(STR), .LD(comparator_9_eq), .CLK(clk), .Q(flash_memory_1_q_dat));
  Register register_2 (
    .D(flash_memory_1_q_dat), .STR(comparator_10_eq), .LD(comparator_11_eq), .CLK(clk),
    .VAL({register_2_val_2, register_2_val}), .Q(flash_memory_1_q_dat));
  _8_By_8_Pixel_Display _8_by_8_pixel_display_1 (
    .CMD(flash_memory_1_q_cmd), .DAT(flash_memory_1_q_dat), .ADR(flash_memory_1_q_adr),
    .OUT_0(_8_by_8_pixel_display_1_out_0), .OUT_1(_8_by_8_pixel_display_1_out_1),
    .OUT_2(_8_by_8_pixel_display_1_out_2), .OUT_3(_8_by_8_pixel_display_1_out_3),
    .OUT_4(_8_by_8_pixel_display_1_out_4), .OUT_5(_8_by_8_pixel_display_1_out_5),
    .OUT_6(_8_by_8_pixel_display_1_out_6), .OUT_7(_8_by_8_pixel_display_1_out_7));
  Seven_Seg_Hex seven_seg_hex_1 (.d(register_2_val_2), .dp(1'b0));
  Seven_Seg_Hex seven_seg_hex_2 (.d(register_2_val), .dp(1'b0));
  LED led_9 (.in(register_2_val_2[3]));
  LED led_10 (.in(_8_by_8_pixel_display_1_out_0[7]));
  LED led_11 (.in(_8_by_8_pixel_display_1_out_1[7]));
  LED led_12 (.in(_8_by_8_pixel_display_1_out_2[7]));
  LED led_13 (.in(_8_by_8_pixel_display_1_out_3[7]));
  LED led_14 (.in(_8_by_8_pixel_display_1_out_4[7]));
  LED led_15 (.in(_8_by_8_pixel_display_1_out_5[7]));
  LED led_16 (.in(_8_by_8_pixel_display_1_out_6[7]));
  LED led_17 (.in(_8_by_8_pixel_display_1_out_7[7]));
  LED led_18 (.in(register_2_val_2[2]));
  LED led_19 (.in(register_2_val_2[1]));
  LED led_20 (.in(_8_by_8_pixel_display_1_out_0[6]));
  LED led_21 (.in(_8_by_8_pixel_display_1_out_0[5]));
  LED led_22 (.in(_8_by_8_pixel_display_1_out_1[6]));
  LED led_23 (.in(_8_by_8_pixel_display_1_out_1[5]));
  LED led_24 (.in(_8_by_8_pixel_display_1_out_2[6]));
  LED led_25 (.in(_8_by_8_pixel_display_1_out_2[5]));
  LED led_26 (.in(_8_by_8_pixel_display_1_out_3[6]));
  LED led_27 (.in(_8_by_8_pixel_display_1_out_3[5]));
  LED led_28 (.in(_8_by_8_pixel_display_1_out_4[6]));
  LED led_29 (.in(_8_by_8_pixel_display_1_out_4[5]));
  LED led_30 (.in(_8_by_8_pixel_display_1_out_5[6]));
  LED led_31 (.in(_8_by_8_pixel_display_1_out_5[5]));
  LED led_32 (.in(_8_by_8_pixel_display_1_out_6[6]));
  LED led_33 (.in(_8_by_8_pixel_display_1_out_6[5]));
  LED led_34 (.in(_8_by_8_pixel_display_1_out_7[6]));
  LED led_35 (.in(_8_by_8_pixel_display_1_out_7[5]));
  LED led_36 (.in(register_2_val_2[0]));
  LED led_37 (.in(register_2_val[3]));
  LED led_38 (.in(_8_by_8_pixel_display_1_out_0[4]));
  LED led_39 (.in(_8_by_8_pixel_display_1_out_0[3]));
  LED led_40 (.in(_8_by_8_pixel_display_1_out_1[4]));
  LED led_41 (.in(_8_by_8_pixel_display_1_out_1[3]));
  LED led_42 (.in(_8_by_8_pixel_display_1_out_2[4]));
  LED led_43 (.in(_8_by_8_pixel_display_1_out_2[3]));
  LED led_44 (.in(_8_by_8_pixel_display_1_out_3[4]));
  LED led_45 (.in(_8_by_8_pixel_display_1_out_3[3]));
  LED led_46 (.in(_8_by_8_pixel_display_1_out_4[4]));
  LED led_47 (.in(_8_by_8_pixel_display_1_out_4[3]));
  LED led_48 (.in(_8_by_8_pixel_display_1_out_5[4]));
  LED led_49 (.in(_8_by_8_pixel_display_1_out_5[3]));
  LED led_50 (.in(_8_by_8_pixel_display_1_out_6[4]));
  LED led_51 (.in(_8_by_8_pixel_display_1_out_6[3]));
  LED led_52 (.in(_8_by_8_pixel_display_1_out_7[4]));
  LED led_53 (.in(_8_by_8_pixel_display_1_out_7[3]));
  LED led_54 (.in(register_2_val[2]));
  LED led_55 (.in(register_2_val[1]));
  LED led_56 (.in(_8_by_8_pixel_display_1_out_0[2]));
  LED led_57 (.in(_8_by_8_pixel_display_1_out_0[1]));
  LED led_58 (.in(_8_by_8_pixel_display_1_out_1[2]));
  LED led_59 (.in(_8_by_8_pixel_display_1_out_1[1]));
  LED led_60 (.in(_8_by_8_pixel_display_1_out_2[2]));
  LED led_61 (.in(_8_by_8_pixel_display_1_out_2[1]));
  LED led_62 (.in(_8_by_8_pixel_display_1_out_3[2]));
  LED led_63 (.in(_8_by_8_pixel_display_1_out_3[1]));
  LED led_64 (.in(_8_by_8_pixel_display_1_out_4[2]));
  LED led_65 (.in(_8_by_8_pixel_display_1_out_4[1]));
  LED led_66 (.in(_8_by_8_pixel_display_1_out_5[2]));
  LED led_67 (.in(_8_by_8_pixel_display_1_out_5[1]));
  LED led_68 (.in(_8_by_8_pixel_display_1_out_6[2]));
  LED led_69 (.in(_8_by_8_pixel_display_1_out_6[1]));
  LED led_70 (.in(_8_by_8_pixel_display_1_out_7[2]));
  LED led_71 (.in(_8_by_8_pixel_display_1_out_7[1]));
  LED led_72 (.in(register_2_val[0]));
  LED led_73 (.in(_8_by_8_pixel_display_1_out_0[0]));
  LED led_74 (.in(_8_by_8_pixel_display_1_out_1[0]));
  LED led_75 (.in(_8_by_8_pixel_display_1_out_2[0]));
  LED led_76 (.in(_8_by_8_pixel_display_1_out_3[0]));
  LED led_77 (.in(_8_by_8_pixel_display_1_out_4[0]));
  LED led_78 (.in(_8_by_8_pixel_display_1_out_5[0]));
  LED led_79 (.in(_8_by_8_pixel_display_1_out_6[0]));
  LED led_80 (.in(_8_by_8_pixel_display_1_out_7[0]));

  // Notes on the sheet:
  //   clk: Hz: 20
  //   CMD
  //   DAT
  //   ADR
  //   CLK
  //   LN: current line of code being executed
  //   DAT_dis
  //   commands requiring the address bus to be disabled:
  //   Bus Transfer:
  //   - load from interface registers
  //   commands requiring the data bus to be disabled:
  //   Storage: 
  //   - load
  //   ALU:
  //   - add
  //   - add with carry
  //   - subtract
  //   incrementor:
  //   - increment
  //   - decrement
  //   logic:
  //   - binary not
  //   - binary or
  //   - binary and
  //   - binary xor
  //   - bitwise not
  //   - bitwise or
  //   - bitwise and
  //   - bitwise xor
  //   a/b/c registers:
  //   - load a
  //   - load b
  //   - load c
  //   compare:
  //   - bigger
  //   - equal
  //   - smaller
  //   flag reg:
  //   - load carry
  //   - load overflow
  //   - load flags
endmodule
