// Digital circuit Comparator.dig as structural Verilog
module Comparator (
  input  [7:0] A,
  input  CMP_bigger,
  input  CMP_equal,
  input  CMP_smaller,
  input  [7:0] B,
  input  CLK,
  output Q
);

  wire and_1_out, and_2_out, and_3_out, comparator_1_eq, comparator_1_gt, comparator_1_lt, or_1_out;

  Comparator #(.Bits(8)) comparator_1 (.a(A), .b(B), .gt(comparator_1_gt), .eq(comparator_1_eq), .lt(comparator_1_lt));
  and and_1 (and_1_out, comparator_1_gt, CMP_bigger);
  and and_2 (and_2_out, comparator_1_eq, CMP_equal);
  and and_3 (and_3_out, comparator_1_lt, CMP_smaller);
  or or_1 (or_1_out, and_1_out, and_2_out, and_3_out);
  // _1bit_Bus_Interface _1bit_bus_interface_1: pin names not known; wires that end beside it: or_1_out, Q

  // Notes on the sheet:
  //   would need the result to be output on the falling edge 
  //   of the clock, where it stays until the next falling edge.
  //   ->  for commands to able to use the result right after 
  //   the command as planned
endmodule
