// Digital circuit Flash Memory.dig as structural Verilog
module Flash_Memory (
  input  [15:0] LN,
  input  DAT_dis,
  input  ADR_dis,
  input  CLK,
  output [7:0] Q_CMD,
  output [7:0] Q_DAT,
  output [15:0] Q_ADR
);

  wire d_ff_1_q, d_ff_2_q, delay_1_out;
  wire [7:0] DAT_d;
  wire [15:0] ADR_d;

  Delay delay_1 (.in(CLK), .out(delay_1_out));
  D_FF d_ff_1 (.D(DAT_dis), .C(delay_1_out), .Q(d_ff_1_q));  // open: nQ
  D_FF d_ff_2 (.D(ADR_dis), .C(delay_1_out), .Q(d_ff_2_q));  // open: nQ
  ROM #(.AddrBits(16), .isProgramMemory("true"), .Bits(8)) CMD (.A(LN), .sel(1'b1), .D(Q_CMD));
  ROM #(.AddrBits(16), .isProgramMemory("true"), .Bits(8)) DAT (.A(LN), .sel(1'b1), .D(DAT_d));
  ROM #(.AddrBits(16), .isProgramMemory("true"), .Bits(16)) ADR (.A(LN), .sel(1'b1), .D(ADR_d));
  assign Q_DAT = d_ff_1_q ? DAT_d : 8'bz;  // Driver driver_1
  assign Q_ADR = d_ff_2_q ? ADR_d : 16'bz;  // Driver driver_2

  // Notes on the sheet:
  //   DAT_dis / ADR_dis :
  //   disable the data / address bus
  //   for the next tick in order to
  //   avoid bus collisions
  //   the clock is delayed in order to wait
  //   for commands to send their disable 
  //   signals before they get saved in order
  //   to instantly stop output to the buses
  //   - at least 16ns delay
  //   contents of CMD (hex, n*v repeats v):
  //   0,6,0,7,18,1a,8,1a,18,a,18,9,1c,b,18,1a,16,22,18,25,28
  //   contents of DAT (hex, n*v repeats v):
  //   0,1,0,0,0,2,0,0,fd,6*0,ff,0,0,1
  //   contents of ADR (hex, n*v repeats v):
  //   0,1,2,1
endmodule
