// Digital circuit Programme Counter.dig as structural Verilog
module Programme_Counter (
  input  [7:0] DAT,
  input  [15:0] ADR,
  input  CLK,
  input  JMP,
  input  CJP,
  input  CLR,
  output [15:0] LN
);

  wire and_1_out, or_1_out, or_2_out;

  or or_1 (or_1_out, DAT[0], DAT[1], DAT[2], DAT[3], DAT[4], DAT[5], DAT[6], DAT[7]);
  and and_1 (and_1_out, or_1_out, CJP);
  or or_2 (or_2_out, JMP, and_1_out);
  CounterPreset #(.maxValue(65535), .Bits(16), .isProgramCounter("true")) counterpreset_1 (
    .en(1'b1), .C(CLK), .dir(1'b0), .in(ADR), .ld(or_2_out), .clr(CLR), .out(LN));  // open: ovf

  // Notes on the sheet:
  //   DAT: Data input
  //   ADR: Address input
  //   CLK: Clock input
  //   JMP: Jump command
  //   CJP: Conditional Jump command
  //   CLR: Clear for starting the CPU
endmodule
