// Digital circuit RAM.dig as structural Verilog
module RAM (
  input  [7:0] DAT_2,
  input  [15:0] ADR_2,
  input  STR_reg1,
  input  STR_reg2,
  input  STR,
  input  LD,
  input  STR_fromaddr,
  input  LD_fromaddr,
  input  LD_toaddr,
  input  CLK,
  output [7:0] DAT,
  output [7:0] ADR
);

  wire d_ff_1_q, d_ff_2_q, d_ff_3_q, not_1_out, not_2_out, or_1_out, or_2_out, or_3_out, or_4_out;
  wire [7:0] ramdualport_1_d, register_1_q, register_2_q;
  wire [15:0] driver_1_out, driver_2_out, or_5_out;

  not not_1 (not_1_out, CLK);
  D_FF d_ff_1 (.D(LD), .C(not_1_out), .Q(d_ff_1_q));  // open: nQ
  D_FF d_ff_2 (.D(LD_fromaddr), .C(not_1_out), .Q(d_ff_2_q));  // open: nQ
  D_FF d_ff_3 (.D(LD_toaddr), .C(not_1_out), .Q(d_ff_3_q));  // open: nQ
  Register #(.Bits(8)) register_1 (.D(DAT_2), .C(STR_reg1), .en(1'b1), .Q(register_1_q));
  Register #(.Bits(8)) register_2 (.D(DAT_2), .C(STR_reg2), .en(1'b1), .Q(register_2_q));
  or or_1 (or_1_out, STR_fromaddr, d_ff_2_q);
  or or_2 (or_2_out, STR_fromaddr, STR);
  or or_3 (or_3_out, d_ff_2_q, d_ff_1_q, d_ff_3_q);
  or or_4 (or_4_out, d_ff_2_q, d_ff_1_q);
  assign driver_1_out = or_1_out ? {register_2_q, register_1_q} : 16'bz;  // Driver driver_1
  assign driver_2_out = not_2_out ? ADR_2 : 16'bz;  // Driver driver_2
  assign or_5_out[7:0] = driver_2_out[7:0] | driver_1_out[7:0];  // Or or_5, 8 bits wide
  not not_2 (not_2_out, or_1_out);
  RAMDualPort #(.AddrBits(16), .Bits(8)) ramdualport_1 (
    .A(or_5_out), .Din(DAT_2), .str(or_2_out), .C(not_1_out), .ld(or_3_out), .D(ramdualport_1_d));
  assign DAT = or_4_out ? ramdualport_1_d : 8'bz;  // Driver driver_3
  assign ADR = d_ff_3_q ? ramdualport_1_d : 8'bz;  // Driver driver_4
  // Pins of 8 and 16 bits meet at or_5_out
  // Pins of 8 and 16 bits meet at driver_1_out
  // Pins of 1 and 16 bits meet at ADR_2
  // Pins of 8 and 16 bits meet at driver_2_out

  // Notes on the sheet:
  //   could be a 
  //   few AND gates
  //   str - store to ram
  //   ld - write to data bus
  //    (output enable)
endmodule
