// Digital circuit Register.dig as structural Verilog
module Register (
  input  [7:0] D,
  input  STR,
  input  LD,
  input  CLK,
  output [7:0] VAL,
  output [7:0] Q
);

  wire and_1_out, d_ff_1_q, delay_1_out, not_1_out;

  not not_1 (not_1_out, CLK);
  Delay delay_1 (.in(CLK), .out(delay_1_out));
  D_FF d_ff_1 (.D(LD), .C(not_1_out), .Q(d_ff_1_q));  // open: nQ
  and and_1 (and_1_out, STR, delay_1_out);
  Register #(.Bits(8)) register_1 (.D(D), .C(and_1_out), .en(1'b1), .Q(VAL));
  assign Q = d_ff_1_q ? VAL : 8'bz;  // Driver driver_1

  // Notes on the sheet:
  //   delay of 8ns - until the setup time of
  //   the dlatch has passed
endmodule
