// Digital circuit Shift Register.dig as structural Verilog
module Shift_Register (
  input  [7:0] A,
  input  STR,
  input  SHR,
  input  SHL,
  input  CLK,
  output [7:0] Q
);

  wire and_1_out, or_2_out;
  wire [7:0] left_out, or_1_out, register_1_q;

  assign or_1_out = Q | A;  // Or or_1, 8 bits wide
  and and_1 (and_1_out, STR, CLK);
  or or_2 (or_2_out, SHR, and_1_out, SHL);
  Register #(.Bits(8)) register_1 (.D(or_1_out), .C(or_2_out), .en(1'b1), .Q(register_1_q));
  BarrelShifter #(.Bits(8)) left (.in(register_1_q), .shift({3'b000, SHL}), .out(left_out));
  BarrelShifter #(.Bits(8), .direction("right")) right (.in(left_out), .shift({3'b000, SHR}), .out(Q));
endmodule
